// Logisim project 04_ARITHMETIC_00_V.circ as structural Verilog: 29 circuits, main circuit main
module main (
  input  [3:0] in_1,
  input  in_2,
  input  in_3,
  input  [3:0] in_4,
  input  in_5,
  input  [3:0] in_6,
  input  [7:0] in_7,
  input  [3:0] in_8,
  input  [7:0] in_9,
  input  [3:0] in_10,
  output [1:0] out_11,
  output out_12,
  output out_13,
  output [1:0] out_14,
  output [7:0] out_15,
  output out_16,
  output out_17
);

  wire addsp2_4_2_carry_out;
  wire [3:0] add1_4_1_output, addb_1_output, adder_1_out, addsp2_4_1_output, addsp2_b_1_output,
       addsptr4_1_output, addt4_1_output, neg4_1_output, negator_1_out, sub4_1_output, sub4d_1_output,
       subtractor_1_out;

  // Probe on in_1
  // Probe on in_1
  // Probe on in_1
  // Probe on in_4
  // Probe on in_4
  // Probe on in_4
  // Probe on in_6
  // Probe on in_6
  // Probe on in_6
  // Probe on in_8
  // Probe on in_8
  // Probe on in_8
  Adder #(.width(4)) adder_1 (.a(in_1), .b(in_4), .out(adder_1_out), .cin(1'b0), .cout(out_12));
  ADDB addb_1 (.Output(addb_1_output), .Input_A(in_1), .Input_B(in_4));
  Subtractor #(.width(4)) subtractor_1 (.a(in_6), .b(in_8), .out(subtractor_1_out), .bin(1'b0), .bout(out_16));
  // Probe on subtractor_1_out
  // Probe on subtractor_1_out
  // Probe on subtractor_1_out
  // Probe on subtractor_1_out
  // Probe on adder_1_out
  // Probe on adder_1_out
  // Probe on adder_1_out
  // Probe on adder_1_out
  // Probe on addb_1_output
  // Probe on addb_1_output
  // Probe on addb_1_output
  // Probe on addb_1_output
  SUB4D sub4d_1 (.Borrow_In(1'b0), .Minuend(in_6), .Subtrahend(in_8), .Output(sub4d_1_output), .Borrow_Out(out_17));
  ADDSP2_4 addsp2_4_1 (.Carry_In(1'b0), .Input_A(in_1), .Output(addsp2_4_1_output), .Input_B(in_4), .Carry_Out(out_13));
  ADDSP2_B addsp2_b_1 (.Input_A(in_1), .Output(addsp2_b_1_output), .Input_B(in_4));
  // Probe on sub4d_1_output
  // Probe on sub4d_1_output
  // Probe on sub4d_1_output
  // Probe on sub4d_1_output
  // Probe on addsp2_4_1_output
  // Probe on addsp2_4_1_output
  // Probe on addsp2_4_1_output
  // Probe on addsp2_4_1_output
  // Probe on addsp2_b_1_output
  // Probe on addsp2_b_1_output
  // Probe on addsp2_b_1_output
  // Probe on addsp2_b_1_output
  SUB4 sub4_1 (.Minuend(in_6), .Subtrahend(in_8), .Output(sub4_1_output));
  ADD1_4 add1_4_1 (.Carry_In(1'b0), .Input_A(in_1), .Input_B(in_4), .Output(add1_4_1_output));  // open: Carry_Out
  // Probe on add1_4_1_output
  // Probe on add1_4_1_output
  // Probe on add1_4_1_output
  // Probe on add1_4_1_output
  ADDT4 addt4_1 (.Carry_In(1'b0), .Input_A(in_1), .Input_B(in_4), .Output(addt4_1_output));  // open: Carry_Out
  // Probe on addt4_1_output
  // Probe on addt4_1_output
  // Probe on addt4_1_output
  // Probe on addt4_1_output
  // Probe on sub4_1_output
  // Probe on sub4_1_output
  // Probe on sub4_1_output
  // Probe on sub4_1_output
  // Probe on in_7
  // Probe on in_9
  ADDSPTR4 addsptr4_1 (.Carry_In(1'b0), .Input_A(in_4), .Input_B(in_1), .Output(addsptr4_1_output));  // open: Carry_Out
  // Probe on addsptr4_1_output
  // Probe on addsptr4_1_output
  // Probe on addsptr4_1_output
  // Probe on addsptr4_1_output
  // Probe on in_10
  // Probe on in_10
  // Probe on in_10
  ADDSP2_4 addsp2_4_2 (
    .Carry_In(in_5), .Input_A(in_7[3:0]), .Output(out_15[3:0]), .Input_B(in_9[3:0]),
    .Carry_Out(addsp2_4_2_carry_out));
  ADDSP2_4 addsp2_4_3 (
    .Carry_In(addsp2_4_2_carry_out), .Input_A(in_7[7:4]), .Output(out_15[7:4]), .Input_B(in_9[7:4]));  // open: Carry_Out
  Negator #(.width(4)) negator_1 (.in(in_10), .out(negator_1_out));
  // Probe on negator_1_out
  // Probe on negator_1_out
  // Probe on negator_1_out
  // Probe on negator_1_out
  ADDSP_V1 addsp_v1_1 (.Input_A(in_2), .Input_B(in_3), .Output(out_11[0]), .Carry_Out(out_11[1]));
  ADDSP addsp_1 (.Input_A(in_2), .Input_B(in_3), .Output(out_14[0]), .Carry_Out(out_14[1]));
  NEG4 neg4_1 (.Input(in_10), .Output(neg4_1_output));
  // Probe on out_15
  // Probe on neg4_1_output
  // Probe on neg4_1_output
  // Probe on neg4_1_output
  // Probe on neg4_1_output
endmodule

module main2 (
);

  wire C0, C1, C2, C3, C4, C5, C6, C7, C8;
  wire [7:0] L1_0, L1_1, L1_2, L1_3, L1_4, L1_5, L1_6, L1_7, L1_8, L2_0, L2_1, L2_2, L2_3, L2_4, L2_5, L2_6,
       L2_7, L2_8, negator_1_out, R0, R1, R2, R3, R4, R5, R6, R7, R8;

  // Probe on L1_0
  // Probe on L1_0
  // Probe on L2_0
  // Probe on L2_0
  // Probe on L1_1
  // Probe on L1_1
  // Probe on L2_1
  // Probe on L2_1
  // Probe on L1_2
  // Probe on L1_2
  // Probe on L2_2
  // Probe on L2_2
  // Probe on C0
  Adder adder_1 (.a(L1_0), .b(L2_0), .out(R0), .cin(1'b0), .cout(C0));
  // Probe on C1
  Adder adder_2 (.a(L1_1), .b(L2_1), .out(R1), .cin(1'b0), .cout(C1));
  // Probe on C2
  Adder adder_3 (.a(L1_2), .b(L2_2), .out(R2), .cin(1'b0), .cout(C2));
  // Probe on R0
  // Probe on R0
  // Probe on R0
  // Probe on R1
  // Probe on R1
  // Probe on R1
  // Probe on R2
  // Probe on R2
  // Probe on R2
  // Probe on L1_6
  // Probe on L1_6
  // Probe on L2_6
  // Probe on L2_6
  // Probe on L1_7
  // Probe on L1_7
  // Probe on L2_7
  // Probe on L2_7
  // Probe on L1_8
  // Probe on L1_8
  // Probe on L2_8
  // Probe on L2_8
  // Probe on C6
  Adder adder_4 (.a(L1_6), .b(L2_6), .out(R6), .cin(1'b0), .cout(C6));
  // Probe on C7
  Adder adder_5 (.a(L1_7), .b(L2_7), .out(R7), .cin(1'b0), .cout(C7));
  // Probe on C8
  Adder adder_6 (.a(L1_8), .b(L2_8), .out(R8), .cin(1'b0), .cout(C8));
  // Probe on L1_3
  // Probe on L1_3
  // Probe on L2_3
  // Probe on L2_3
  // Probe on L1_4
  // Probe on L1_4
  // Probe on L2_4
  // Probe on L2_4
  // Probe on L1_5
  // Probe on L1_5
  // Probe on L2_5
  // Probe on L2_5
  Adder adder_7 (.a(L1_3), .b(L2_3), .out(R3), .cin(1'b0), .cout(C3));
  Adder adder_8 (.a(L1_4), .b(L2_4), .out(R4), .cin(1'b0), .cout(C4));
  Adder adder_9 (.a(L1_5), .b(L2_5), .out(R5), .cin(1'b0), .cout(C5));
  // Probe on R6
  // Probe on R6
  // Probe on R6
  // Probe on R7
  // Probe on R7
  // Probe on R7
  // Probe on R8
  // Probe on R8
  // Probe on R8
  // Probe on C3
  // Probe on C4
  // Probe on C5
  Negator negator_1 (.in(R7), .out(negator_1_out));
  // Probe on R3
  // Probe on R3
  // Probe on R3
  // Probe on R4
  // Probe on R4
  // Probe on R4
  // Probe on R5
  // Probe on R5
  // Probe on R5
  // Probe on negator_1_out
  // Probe on negator_1_out
  // Probe on negator_1_out
  // Probe on L1_0
  // Probe on L2_0
  // Probe on R0
  // Probe on C0
  // Probe on L1_1
  // Probe on L2_1
  // Probe on R1
  // Probe on C1
  // Probe on L1_2
  // Probe on L2_2
  // Probe on R2
  // Probe on C2
  // Probe on L1_3
  // Probe on L2_3
  // Probe on R3
  // Probe on C3
  // Probe on L1_4
  // Probe on L2_4
  // Probe on R4
  // Probe on C4
  // Probe on L1_0
  // Probe on L2_0
  // Probe on R0
  // Probe on L1_1
  // Probe on L2_1
  // Probe on R1
  // Probe on L1_2
  // Probe on L2_2
  // Probe on R2
  // Probe on L1_3
  // Probe on L2_3
  // Probe on R3
  // Probe on L1_4
  // Probe on L2_4
  // Probe on R4
  // Probe on L1_5
  // Probe on L2_5
  // Probe on R5
  // Probe on C5
  // Probe on L1_6
  // Probe on L2_6
  // Probe on R6
  // Probe on C6
  // Probe on L1_7
  // Probe on L2_7
  // Probe on R7
  // Probe on C7
  // Probe on L1_8
  // Probe on L2_8
  // Probe on R8
  // Probe on C8
  // Probe on L1_5
  // Probe on L2_5
  // Probe on R5
  // Probe on L1_6
  // Probe on L2_6
  // Probe on R6
  // Probe on L1_7
  // Probe on L2_7
  // Probe on R7
  // Probe on L1_8
  // Probe on L2_8
  // Probe on R8
  list1 list1_1 (
    .out_1(L1_0), .out_2(L1_1), .out_3(L1_2), .out_4(L1_3), .out_5(L1_4), .out_6(L1_5), .out_7(L1_6),
    .out_8(L1_7), .out_9(L1_8));
  list2 list2_1 (
    .out_1(L2_0), .out_2(L2_1), .out_3(L2_2), .out_4(L2_3), .out_5(L2_4), .out_6(L2_5), .out_7(L2_6),
    .out_8(L2_7), .out_9(L2_8));
endmodule

module ADD0 (
  input  Carry_In,
  input  Input_A,
  input  Input_B,
  output Output,
  output Carry_Out
);

  wire and_1_out, and_2_out, nor_1_out, nor_2_out, nor_3_out;

  nor nor_1 (nor_1_out, Input_A, Input_B);
  nor nor_2 (nor_2_out, nor_1_out, and_1_out);
  and and_1 (and_1_out, Input_A, Input_B);
  nor nor_3 (nor_3_out, Carry_In, nor_2_out);
  and and_2 (and_2_out, Carry_In, nor_2_out);
  nor nor_4 (Output, nor_3_out, and_2_out);
  or or_1 (Carry_Out, and_2_out, and_1_out);

  // Notes on the sheet:
  //   0+0=0 (R=0)
  //   0+1=1 (R=0)
  //   1+0=1 (R=0)
  //   1+1=0 (R=1)
endmodule

module ADD1 (
  input  Carry_In,
  input  Input_A,
  input  Input_B,
  output Output,
  output Carry_Out
);

  wire and_1_out, and_2_out, xor_1_out;

  xor xor_1 (xor_1_out, Input_A, Input_B);
  and and_1 (and_1_out, Input_A, Input_B);
  xor xor_2 (Output, Carry_In, xor_1_out);
  and and_2 (and_2_out, Carry_In, xor_1_out);
  or or_1 (Carry_Out, and_2_out, and_1_out);
endmodule

module ADD1_4 (
  input  Carry_In,
  input  [3:0] Input_A,
  input  [3:0] Input_B,
  output [3:0] Output,
  output Carry_Out
);

  wire add1_1_carry_out, add1_2_carry_out, add1_3_carry_out;

  ADD1 add1_1 (
    .Carry_In(Carry_In), .Input_A(Input_A[0]), .Input_B(Input_B[0]), .Output(Output[0]),
    .Carry_Out(add1_1_carry_out));
  ADD1 add1_2 (
    .Carry_In(add1_1_carry_out), .Input_A(Input_A[1]), .Input_B(Input_B[1]), .Output(Output[1]),
    .Carry_Out(add1_2_carry_out));
  ADD1 add1_3 (
    .Carry_In(add1_2_carry_out), .Input_A(Input_A[2]), .Input_B(Input_B[2]), .Output(Output[2]),
    .Carry_Out(add1_3_carry_out));
  ADD1 add1_4 (
    .Carry_In(add1_3_carry_out), .Input_A(Input_A[3]), .Input_B(Input_B[3]), .Output(Output[3]),
    .Carry_Out(Carry_Out));
endmodule

module ADDB (
  input  [3:0] Input_A,
  input  [3:0] Input_B,
  output [3:0] Output
);

  wire and_1_out, and_2_out, and_3_out, and_4_out, and_6_out, and_7_out, and_8_out, and_9_out, and_10_out,
       and_11_out, not_1_out, not_2_out, not_3_out, not_4_out, not_5_out, not_6_out, not_7_out, or_1_out,
       or_2_out, or_3_out, or_4_out, or_5_out, or_6_out, or_7_out, or_8_out, or_9_out;

  or or_1 (or_1_out, Input_A[0], Input_B[0]);
  and and_1 (and_1_out, Input_A[0], Input_B[0]);
  or or_2 (or_2_out, Input_A[1], Input_B[1]);
  and and_2 (and_2_out, Input_A[1], Input_B[1]);
  or or_3 (or_3_out, Input_A[2], Input_B[2]);
  and and_3 (and_3_out, Input_A[2], Input_B[2]);
  or or_4 (or_4_out, Input_A[3], Input_B[3]);
  and and_4 (and_4_out, Input_A[3], Input_B[3]);
  not not_1 (not_1_out, and_1_out);
  not not_2 (not_2_out, and_2_out);
  or or_5 (or_5_out, and_6_out, and_2_out);
  not not_3 (not_3_out, and_3_out);
  or or_6 (or_6_out, and_8_out, and_3_out);
  not not_4 (not_4_out, and_4_out);
  and and_5 (Output[0], or_1_out, not_1_out);
  or or_7 (or_7_out, and_1_out, and_7_out);
  and and_6 (and_6_out, and_1_out, and_7_out);
  and and_7 (and_7_out, or_2_out, not_2_out);
  or or_8 (or_8_out, or_5_out, and_9_out);
  and and_8 (and_8_out, or_5_out, and_9_out);
  and and_9 (and_9_out, or_3_out, not_3_out);
  or or_9 (or_9_out, or_6_out, and_11_out);
  and and_10 (and_10_out, or_6_out, and_11_out);
  and and_11 (and_11_out, or_4_out, not_4_out);
  and and_12 (Output[1], or_7_out, not_5_out);
  not not_5 (not_5_out, and_6_out);
  and and_13 (Output[2], or_8_out, not_6_out);
  not not_6 (not_6_out, and_8_out);
  and and_14 (Output[3], or_9_out, not_7_out);
  not not_7 (not_7_out, and_10_out);
endmodule

module ADD2 (
  input  Carry_In,
  input  Input_A,
  input  Input_B,
  output Output,
  output Carry_Out
);

  wire and_1_out, and_2_out, and_3_out, not_1_out, not_2_out, or_1_out, or_2_out;

  or or_1 (or_1_out, Input_A, Input_B);
  and and_1 (and_1_out, Input_A, Input_B);
  not not_1 (not_1_out, and_1_out);
  or or_2 (or_2_out, Carry_In, and_3_out);
  and and_2 (and_2_out, Carry_In, and_3_out);
  and and_3 (and_3_out, or_1_out, not_1_out);
  not not_2 (not_2_out, and_2_out);
  or or_3 (Carry_Out, and_2_out, and_1_out);
  and and_4 (Output, or_2_out, not_2_out);

  // Notes on the sheet:
  //   0+0=0 (R=0)
  //   0+1=1 (R=0)
  //   1+0=1 (R=0)
  //   1+1=0 (R=1)
endmodule

module ADDSP_V1 (
  input  Input_A,
  input  Input_B,
  output Output,
  output Carry_Out
);

  wire not_1_out, or_1_out;

  or or_1 (or_1_out, Input_A, Input_B);
  and and_1 (Carry_Out, Input_A, Input_B);
  and and_2 (Output, or_1_out, not_1_out);
  not not_1 (not_1_out, Carry_Out);

  // Notes on the sheet:
  //   0+0=0 (R=0)
  //   0+1=1 (R=0)
  //   1+0=1 (R=0)
  //   1+1=0 (R=1)
endmodule

module ADDSP (
  input  Input_A,
  input  Input_B,
  output Output,
  output Carry_Out
);

  wire nor_1_out;

  nor nor_1 (nor_1_out, Input_A, Input_B);
  and and_1 (Carry_Out, Input_A, Input_B);
  nor nor_2 (Output, nor_1_out, Carry_Out);

  // Notes on the sheet:
  //   0+0=0 (R=0)
  //   0+1=1 (R=0)
  //   1+0=1 (R=0)
  //   1+1=0 (R=1)
endmodule

module ADDSP2 (
  input  Carry_In,
  input  Input_A,
  input  Input_B,
  output Output,
  output Carry_Out
);

  wire addsp_1_carry_out, addsp_2_carry_out, addsp_2_output;

  ADDSP addsp_1 (.Input_A(Carry_In), .Input_B(addsp_2_output), .Output(Output), .Carry_Out(addsp_1_carry_out));
  ADDSP addsp_2 (.Input_A(Input_A), .Input_B(Input_B), .Output(addsp_2_output), .Carry_Out(addsp_2_carry_out));
  or or_1 (Carry_Out, addsp_1_carry_out, addsp_2_carry_out);

  // Notes on the sheet:
  //   C_IN
  //   C_ABIN
  //   V_AB
  //   A
  //   B
  //   C_AB
  //   0+0=0 (R=0)
  //   0+1=1 (R=0)
  //   1+0=1 (R=0)
  //   1+1=0 (R=1)
  //   V_OUT
  //   C_OUT
endmodule

module ADDSP_B (
  input  [3:0] Input_A,
  input  [3:0] Input_B,
  output [3:0] Output
);

  wire addsp_1_carry_out, addsp_2_carry_out, addsp_2_output, addsp_3_carry_out, addsp_3_output,
       addsp_4_output, addsp_5_carry_out, addsp_6_carry_out, or_1_out, or_2_out;

  ADDSP addsp_1 (.Input_A(Input_A[0]), .Input_B(Input_B[0]), .Output(Output[0]), .Carry_Out(addsp_1_carry_out));
  ADDSP addsp_2 (.Input_A(Input_A[1]), .Input_B(Input_B[1]), .Output(addsp_2_output), .Carry_Out(addsp_2_carry_out));
  ADDSP addsp_3 (.Input_A(Input_A[2]), .Input_B(Input_B[2]), .Output(addsp_3_output), .Carry_Out(addsp_3_carry_out));
  ADDSP addsp_4 (.Input_A(Input_A[3]), .Input_B(Input_B[3]), .Output(addsp_4_output));  // open: Carry_Out
  ADDSP addsp_5 (
    .Input_A(addsp_1_carry_out), .Input_B(addsp_2_output), .Output(Output[1]), .Carry_Out(addsp_5_carry_out));
  or or_1 (or_1_out, addsp_5_carry_out, addsp_2_carry_out);
  ADDSP addsp_6 (.Input_A(or_1_out), .Input_B(addsp_3_output), .Output(Output[2]), .Carry_Out(addsp_6_carry_out));
  or or_2 (or_2_out, addsp_6_carry_out, addsp_3_carry_out);
  ADDSP addsp_7 (.Input_A(or_2_out), .Input_B(addsp_4_output), .Output(Output[3]));  // open: Carry_Out
endmodule

module ADDSP2_B (
  input  [3:0] Input_A,
  input  [3:0] Input_B,
  output [3:0] Output
);

  wire addsp2_1_carry_out, addsp2_2_carry_out, addsp2_3_carry_out;

  ADDSP2 addsp2_1 (
    .Carry_In(1'b0), .Input_A(Input_A[0]), .Input_B(Input_B[0]), .Output(Output[0]),
    .Carry_Out(addsp2_1_carry_out));
  ADDSP2 addsp2_2 (
    .Carry_In(addsp2_1_carry_out), .Input_A(Input_A[1]), .Input_B(Input_B[1]), .Output(Output[1]),
    .Carry_Out(addsp2_2_carry_out));
  ADDSP2 addsp2_3 (
    .Carry_In(addsp2_2_carry_out), .Input_A(Input_A[2]), .Input_B(Input_B[2]), .Output(Output[2]),
    .Carry_Out(addsp2_3_carry_out));
  ADDSP2 addsp2_4 (
    .Carry_In(addsp2_3_carry_out), .Input_A(Input_A[3]), .Input_B(Input_B[3]), .Output(Output[3]));  // open: Carry_Out
endmodule

module ADDSP2_4 (
  input  Carry_In,
  input  [3:0] Input_A,
  input  [3:0] Input_B,
  output [3:0] Output,
  output Carry_Out
);

  wire addsp2_1_carry_out, addsp2_2_carry_out, addsp2_3_carry_out;

  ADDSP2 addsp2_1 (
    .Carry_In(Carry_In), .Input_A(Input_A[0]), .Input_B(Input_B[0]), .Output(Output[0]),
    .Carry_Out(addsp2_1_carry_out));
  ADDSP2 addsp2_2 (
    .Carry_In(addsp2_1_carry_out), .Input_A(Input_A[1]), .Input_B(Input_B[1]), .Output(Output[1]),
    .Carry_Out(addsp2_2_carry_out));
  ADDSP2 addsp2_3 (
    .Carry_In(addsp2_2_carry_out), .Input_A(Input_A[2]), .Input_B(Input_B[2]), .Output(Output[2]),
    .Carry_Out(addsp2_3_carry_out));
  ADDSP2 addsp2_4 (
    .Carry_In(addsp2_3_carry_out), .Input_A(Input_A[3]), .Input_B(Input_B[3]), .Output(Output[3]),
    .Carry_Out(Carry_Out));

  // Notes on the sheet:
  //   0+0=0 (R=0)
  //   0+1=1 (R=0)
  //   1+0=1 (R=0)
  //   1+1=0 (R=1)
endmodule

module ADDSPTR (
  input  Input_A,
  input  Input_B,
  output Output,
  output Carry_Out
);

  wire pull_resistor_8_node, transistor_1_out, transistor_2_out, transistor_3_out, transistor_4_out,
       transistor_5_out, transistor_6_out, transistor_11_out, transistor_13_out, transistor_14_out,
       transistor_15_out, transistor_18_out;

  Transistor transistor_1 (.in(1'b1), .out(transistor_1_out), .gate(Input_A));
  Transistor #(.\type ("n")) transistor_2 (.in(transistor_1_out), .out(transistor_2_out), .gate(Input_A));
  Transistor #(.\type ("n"), .gate("br")) transistor_3 (.in(transistor_2_out), .out(transistor_3_out), .gate(Input_B));
  Transistor #(.gate("br")) transistor_4 (.in(1'b1), .out(transistor_4_out), .gate(Input_A));
  Transistor transistor_5 (.in(transistor_4_out), .out(transistor_5_out), .gate(Input_B));
  Transistor #(.\type ("n"), .gate("br")) transistor_6 (.in(transistor_5_out), .out(transistor_6_out), .gate(Input_A));
  Transistor #(.\type ("n")) transistor_7 (.in(transistor_5_out), .out(transistor_6_out), .gate(Input_B));
  Transistor #(.gate("br")) transistor_8 (.in(1'b1), .out(transistor_1_out), .gate(Input_B));
  Pull_Resistor pull_resistor_1 (.node(transistor_2_out));
  Pull_Resistor pull_resistor_2 (.node(transistor_1_out));
  Pull_Resistor pull_resistor_3 (.node(transistor_5_out));
  Pull_Resistor pull_resistor_4 (.node(transistor_4_out));
  Transistor transistor_9 (.in(1'b1), .out(Carry_Out), .gate(transistor_1_out));
  Pull_Resistor pull_resistor_5 (.node(Carry_Out));
  Transistor #(.\type ("n")) transistor_10 (.in(Carry_Out), .out(transistor_3_out), .gate(transistor_1_out));
  Transistor transistor_11 (.in(1'b1), .out(transistor_11_out), .gate(transistor_5_out));
  Pull_Resistor pull_resistor_6 (.node(transistor_11_out));
  Transistor #(.\type ("n")) transistor_12 (.in(transistor_11_out), .out(transistor_6_out), .gate(transistor_5_out));
  Transistor transistor_13 (.in(1'b1), .out(transistor_13_out), .gate(Carry_Out));
  Pull_Resistor pull_resistor_7 (.node(transistor_13_out));
  Transistor #(.\type ("n")) transistor_14 (.in(transistor_13_out), .out(transistor_14_out), .gate(Carry_Out));
  Transistor #(.gate("br")) transistor_15 (.in(1'b1), .out(transistor_15_out), .gate(transistor_13_out));
  Transistor transistor_16 (.in(1'b1), .out(transistor_15_out), .gate(transistor_11_out));
  Pull_Resistor pull_resistor_8 (.node(pull_resistor_8_node));
  Transistor #(.\type ("n")) transistor_17 (
    .in(transistor_15_out), .out(pull_resistor_8_node), .gate(transistor_11_out));
  Transistor #(.\type ("n"), .gate("br")) transistor_18 (
    .in(pull_resistor_8_node), .out(transistor_18_out), .gate(transistor_13_out));
  Pull_Resistor pull_resistor_9 (.node(transistor_15_out));
  Transistor transistor_19 (.in(1'b1), .out(Output), .gate(transistor_15_out));
  Pull_Resistor pull_resistor_10 (.node(Output));
  Transistor #(.\type ("n")) transistor_20 (.in(Output), .out(transistor_18_out), .gate(transistor_15_out));
  // also tied to GND on the sheet: {transistor_3_out, transistor_6_out, transistor_14_out, transistor_18_out}

  // Notes on the sheet:
  //   NON-ET
  //   NON-OU
  //   NON
  //   NON
  //   ET
  //   NON
  //   OU
  //   NON-ET
  //   NON
  //   ET
endmodule

module ADDSPTR2 (
  input  Carry_In,
  input  Input_A,
  input  Input_B,
  output Output,
  output Carry_Out
);

  wire addsptr_1_carry_out, addsptr_1_output, addsptr_2_carry_out;

  ADDSPTR addsptr_1 (.Input_A(Input_A), .Input_B(Input_B), .Output(addsptr_1_output), .Carry_Out(addsptr_1_carry_out));
  ADDSPTR addsptr_2 (.Input_A(Carry_In), .Input_B(addsptr_1_output), .Output(Output), .Carry_Out(addsptr_2_carry_out));
  OU ou_1 (.in_1(addsptr_2_carry_out), .in_2(addsptr_1_carry_out), .out_3(Carry_Out));
endmodule

module ADDSPTR4 (
  input  Carry_In,
  input  [3:0] Input_A,
  input  [3:0] Input_B,
  output [3:0] Output,
  output Carry_Out
);

  wire addsptr2_1_carry_out, addsptr2_2_carry_out, addsptr2_3_carry_out;

  ADDSPTR2 addsptr2_1 (
    .Carry_In(Carry_In), .Input_A(Input_A[0]), .Input_B(Input_B[0]), .Output(Output[0]),
    .Carry_Out(addsptr2_1_carry_out));
  ADDSPTR2 addsptr2_2 (
    .Carry_In(addsptr2_1_carry_out), .Input_A(Input_A[1]), .Input_B(Input_B[1]), .Output(Output[1]),
    .Carry_Out(addsptr2_2_carry_out));
  ADDSPTR2 addsptr2_3 (
    .Carry_In(addsptr2_2_carry_out), .Input_A(Input_A[2]), .Input_B(Input_B[2]), .Output(Output[2]),
    .Carry_Out(addsptr2_3_carry_out));
  ADDSPTR2 addsptr2_4 (
    .Carry_In(addsptr2_3_carry_out), .Input_A(Input_A[3]), .Input_B(Input_B[3]), .Output(Output[3]),
    .Carry_Out(Carry_Out));
endmodule

module ADDTR (
  input  Carry_In,
  input  Input_A,
  input  Input_B,
  output Output,
  output Carry_Out
);

  wire pull_resistor_1_node, transistor_1_out, transistor_4_out, transistor_5_out, transistor_6_out,
       transistor_7_out, transistor_9_out, transistor_11_out, transistor_12_out, transistor_13_out,
       transistor_15_out, transistor_16_out, transistor_17_out, transistor_18_out, transistor_19_out,
       transistor_20_out, transistor_22_out, transistor_23_out, transistor_24_out, transistor_26_out,
       transistor_31_out, transistor_33_out;

  Transistor #(.gate("br")) transistor_1 (.in(1'b1), .out(transistor_1_out), .gate(Input_B));
  Transistor transistor_2 (.in(1'b1), .out(transistor_1_out), .gate(Input_A));
  Pull_Resistor pull_resistor_1 (.node(pull_resistor_1_node));
  Transistor #(.\type ("n")) transistor_3 (.in(transistor_1_out), .out(pull_resistor_1_node), .gate(Input_A));
  Transistor #(.\type ("n"), .gate("br")) transistor_4 (
    .in(pull_resistor_1_node), .out(transistor_4_out), .gate(Input_B));
  Transistor #(.gate("br")) transistor_5 (.in(1'b1), .out(transistor_5_out), .gate(Input_A));
  Transistor transistor_6 (.in(transistor_5_out), .out(transistor_6_out), .gate(Input_B));
  Transistor #(.\type ("n")) transistor_7 (.in(transistor_6_out), .out(transistor_7_out), .gate(Input_B));
  Transistor #(.\type ("n"), .gate("br")) transistor_8 (.in(transistor_6_out), .out(transistor_7_out), .gate(Input_A));
  Pull_Resistor pull_resistor_2 (.node(transistor_1_out));
  Pull_Resistor pull_resistor_3 (.node(transistor_6_out));
  Pull_Resistor pull_resistor_4 (.node(transistor_5_out));
  Transistor transistor_9 (.in(1'b1), .out(transistor_9_out), .gate(transistor_1_out));
  Pull_Resistor pull_resistor_5 (.node(transistor_9_out));
  Transistor #(.\type ("n")) transistor_10 (.in(transistor_9_out), .out(transistor_4_out), .gate(transistor_1_out));
  Transistor #(.gate("br")) transistor_11 (.in(1'b1), .out(transistor_11_out), .gate(transistor_6_out));
  Transistor transistor_12 (.in(transistor_11_out), .out(transistor_12_out), .gate(transistor_9_out));
  Transistor #(.\type ("n")) transistor_13 (.in(transistor_12_out), .out(transistor_13_out), .gate(transistor_9_out));
  Pull_Resistor pull_resistor_6 (.node(transistor_11_out));
  Transistor #(.\type ("n"), .gate("br")) transistor_14 (
    .in(transistor_12_out), .out(transistor_13_out), .gate(transistor_6_out));
  Pull_Resistor pull_resistor_7 (.node(transistor_12_out));
  Transistor transistor_15 (.in(1'b1), .out(transistor_15_out), .gate(Carry_In));
  Transistor #(.\type ("n")) transistor_16 (.in(transistor_15_out), .out(transistor_16_out), .gate(Carry_In));
  Transistor #(.\type ("n"), .gate("br")) transistor_17 (
    .in(transistor_16_out), .out(transistor_17_out), .gate(transistor_12_out));
  Transistor #(.gate("br")) transistor_18 (.in(1'b1), .out(transistor_18_out), .gate(Carry_In));
  Transistor transistor_19 (.in(transistor_18_out), .out(transistor_19_out), .gate(transistor_12_out));
  Transistor #(.\type ("n")) transistor_20 (.in(transistor_19_out), .out(transistor_20_out), .gate(transistor_12_out));
  Transistor #(.gate("br")) transistor_21 (.in(1'b1), .out(transistor_15_out), .gate(transistor_12_out));
  Pull_Resistor pull_resistor_8 (.node(transistor_15_out));
  Pull_Resistor pull_resistor_9 (.node(transistor_16_out));
  Transistor #(.gate("br")) transistor_22 (.in(1'b1), .out(transistor_22_out), .gate(transistor_26_out));
  Transistor transistor_23 (.in(transistor_22_out), .out(transistor_23_out), .gate(transistor_9_out));
  Transistor #(.\type ("n")) transistor_24 (.in(transistor_23_out), .out(transistor_24_out), .gate(transistor_9_out));
  Transistor #(.\type ("n"), .gate("br")) transistor_25 (
    .in(transistor_19_out), .out(transistor_20_out), .gate(Carry_In));
  Transistor transistor_26 (.in(1'b1), .out(transistor_26_out), .gate(transistor_15_out));
  Transistor #(.\type ("n")) transistor_27 (.in(transistor_26_out), .out(transistor_17_out), .gate(transistor_15_out));
  Pull_Resistor pull_resistor_10 (.node(transistor_23_out));
  Pull_Resistor pull_resistor_11 (.node(transistor_22_out));
  Transistor #(.\type ("n"), .gate("br")) transistor_28 (
    .in(transistor_23_out), .out(transistor_24_out), .gate(transistor_26_out));
  Pull_Resistor pull_resistor_12 (.node(transistor_19_out));
  Pull_Resistor pull_resistor_13 (.node(transistor_18_out));
  Pull_Resistor pull_resistor_14 (.node(transistor_26_out));
  Transistor transistor_29 (.in(1'b1), .out(Carry_Out), .gate(transistor_23_out));
  Transistor #(.\type ("n")) transistor_30 (.in(Carry_Out), .out(transistor_24_out), .gate(transistor_23_out));
  Transistor #(.gate("br")) transistor_31 (.in(1'b1), .out(transistor_31_out), .gate(transistor_19_out));
  Transistor transistor_32 (.in(transistor_31_out), .out(Output), .gate(transistor_26_out));
  Transistor #(.\type ("n"), .gate("br")) transistor_33 (
    .in(Output), .out(transistor_33_out), .gate(transistor_19_out));
  Transistor #(.\type ("n")) transistor_34 (.in(Output), .out(transistor_33_out), .gate(transistor_26_out));
  Pull_Resistor pull_resistor_15 (.node(Carry_Out));
  Pull_Resistor pull_resistor_16 (.node(transistor_31_out));
  Pull_Resistor pull_resistor_17 (.node(Output));
  // also tied to GND on the sheet: {transistor_4_out, transistor_7_out, transistor_13_out, transistor_20_out, transistor_17_out, transistor_24_out, transistor_33_out}

  // Notes on the sheet:
  //   NON-ET
  //   NON-OU
  //   NON
  //   ET
  //   NON-OU
  //   NON-ET
  //   NON-OU
  //   NON
  //   NON-OU
  //   ET
  //   NON
  //   NON-OU
  //   OU
endmodule

module ADDT4 (
  input  Carry_In,
  input  [3:0] Input_A,
  input  [3:0] Input_B,
  output [3:0] Output,
  output Carry_Out
);

  wire addtr_1_carry_out, addtr_2_carry_out, addtr_3_carry_out;

  ADDTR addtr_1 (
    .Carry_In(Carry_In), .Input_A(Input_A[0]), .Input_B(Input_B[0]), .Output(Output[0]),
    .Carry_Out(addtr_1_carry_out));
  ADDTR addtr_2 (
    .Carry_In(addtr_1_carry_out), .Input_A(Input_A[1]), .Input_B(Input_B[1]), .Output(Output[1]),
    .Carry_Out(addtr_2_carry_out));
  ADDTR addtr_3 (
    .Carry_In(addtr_2_carry_out), .Input_A(Input_A[2]), .Input_B(Input_B[2]), .Output(Output[2]),
    .Carry_Out(addtr_3_carry_out));
  ADDTR addtr_4 (
    .Carry_In(addtr_3_carry_out), .Input_A(Input_A[3]), .Input_B(Input_B[3]), .Output(Output[3]),
    .Carry_Out(Carry_Out));
endmodule

module NEG4 (
  input  [3:0] Input,
  output [3:0] Output
);

  wire [3:0] not_1_out;

  assign not_1_out = ~Input;  // NOT_Gate not_1, 4 bits wide
  Adder #(.width(4)) adder_1 (.a(not_1_out), .b(4'b0001), .out(Output), .cin(1'b0));  // open: cout
endmodule

module NEG42 (
  input  [3:0] Input,
  output [3:0] Output
);

  wire [3:0] xor_1_out;

  assign xor_1_out = 4'b1111 ^ Input;  // XOR_Gate xor_1, 4 bits wide
  Adder #(.width(4)) adder_1 (.a(xor_1_out), .b(4'b0001), .out(Output), .cin(1'b0));  // open: cout
endmodule

module SUB4 (
  input  [3:0] Minuend,
  input  [3:0] Subtrahend,
  output [3:0] Output
);

  wire [3:0] negator_1_out;

  Negator #(.width(4)) negator_1 (.in(Subtrahend), .out(negator_1_out));
  Adder #(.width(4)) adder_1 (.a(Minuend), .b(negator_1_out), .out(Output), .cin(1'b0));  // open: cout
endmodule

module SUB4D (
  input  Borrow_In,
  input  [3:0] Minuend,
  input  [3:0] Subtrahend,
  output [3:0] Output,
  output Borrow_Out
);

  wire [3:0] adder_1_out;
  wire [4:0] negator_1_out;

  Adder #(.width(4)) adder_1 (.a({3'b000, Borrow_In}), .b(Subtrahend), .out(adder_1_out), .cin(1'b0));  // open: cout
  Negator #(.width(5)) negator_1 (.in({1'b0, adder_1_out}), .out(negator_1_out));
  Adder #(.width(5)) adder_2 (
    .a({1'b0, Minuend}), .b(negator_1_out), .out({Borrow_Out, Output}), .cin(1'b0));  // open: cout
endmodule

module SUB1 (
  input  Carry_In,
  input  Input_A,
  input  Input_B,
  output Output,
  output Carry_Out
);

  wire and_1_out, and_2_out, and_3_out, and_4_out, nor_1_out, nor_2_out, nor_3_out, not_1_out, not_2_out;

  nor nor_1 (nor_1_out, Input_A, Input_B);
  nor nor_2 (nor_2_out, nor_1_out, and_1_out);
  and and_1 (and_1_out, Input_A, Input_B);
  not not_1 (not_1_out, nor_2_out);
  not not_2 (not_2_out, Input_A);
  nor nor_3 (nor_3_out, Carry_In, nor_2_out);
  nor nor_4 (Output, nor_3_out, and_2_out);
  and and_2 (and_2_out, Carry_In, nor_2_out);
  and and_3 (and_3_out, Carry_In, not_1_out);
  or or_1 (Carry_Out, and_3_out, and_4_out);
  and and_4 (and_4_out, not_2_out, Input_B);
endmodule

module SUB2 (
  input  Carry_In,
  input  Input_A,
  input  Input_B,
  output Output,
  output Carry_Out
);

  wire addsp_1_output, and_1_out, and_2_out, not_1_out, not_2_out;

  ADDSP addsp_1 (.Input_A(Input_A), .Input_B(Input_B), .Output(addsp_1_output));  // open: Carry_Out
  not not_1 (not_1_out, addsp_1_output);
  not not_2 (not_2_out, Input_A);
  ADDSP addsp_2 (.Input_A(Carry_In), .Input_B(addsp_1_output), .Output(Output));  // open: Carry_Out
  and and_1 (and_1_out, Carry_In, not_1_out);
  or or_1 (Carry_Out, and_1_out, and_2_out);
  and and_2 (and_2_out, not_2_out, Input_B);
endmodule

module list1 (
  output [7:0] out_1,
  output [7:0] out_2,
  output [7:0] out_3,
  output [7:0] out_4,
  output [7:0] out_5,
  output [7:0] out_6,
  output [7:0] out_7,
  output [7:0] out_8,
  output [7:0] out_9
);

  // Probe on 8'h5
  // Probe on 8'h7
  // Probe on 8'h14
  // Probe on 8'hf1
  // Probe on 8'h5
  // Probe on 8'h14
  // Probe on 8'h32
  // Probe on 8'h73
  // Probe on 8'h92

  assign out_1 = 8'h5;
  assign out_2 = 8'h7;
  assign out_3 = 8'h14;
  assign out_4 = 8'hf1;
  assign out_5 = 8'h5;
  assign out_6 = 8'h14;
  assign out_7 = 8'h32;
  assign out_8 = 8'h73;
  assign out_9 = 8'h92;
endmodule

module list2 (
  output [7:0] out_1,
  output [7:0] out_2,
  output [7:0] out_3,
  output [7:0] out_4,
  output [7:0] out_5,
  output [7:0] out_6,
  output [7:0] out_7,
  output [7:0] out_8,
  output [7:0] out_9
);

  // Probe on 8'h5
  // Probe on 8'h7
  // Probe on 8'h14
  // Probe on 8'ha
  // Probe on 8'hec
  // Probe on 8'hf1
  // Probe on 8'h32
  // Probe on 8'h73
  // Probe on 8'h92

  assign out_1 = 8'h5;
  assign out_2 = 8'h7;
  assign out_3 = 8'h14;
  assign out_4 = 8'ha;
  assign out_5 = 8'hec;
  assign out_6 = 8'hf1;
  assign out_7 = 8'h32;
  assign out_8 = 8'h73;
  assign out_9 = 8'h92;
endmodule

module main_ADD_OU_EX (
  input  Input_A,
  input  Input_A_2,
  input  A,
  input  Input_B,
  input  Input_B_2,
  input  B,
  input  Input_A_3,
  input  Input_A_4,
  input  Input_B_3,
  input  Input_B_4,
  input  Input_A_5,
  input  Input_B_5,
  input  Input_A_6,
  input  Input_B_6,
  output Output,
  output Output_2,
  output Carry_Out,
  output Carry_Out_2,
  output out_19,
  output Output_3,
  output Output_4,
  output out_22,
  output Carry_Out_3,
  output Carry_Out_4,
  output out_25,
  output Output_5,
  output Carry_Out_5,
  output out_28,
  output Output_6,
  output Carry_Out_6
);

  wire and_2_out, and_10_out, and_12_out, and_13_out, nand_1_out, nand_2_out, nor_1_out, nor_2_out,
       nor_5_out, not_1_out, not_2_out, not_3_out, or_1_out, or_2_out, or_3_out, or_4_out, or_5_out;

  or or_1 (or_1_out, Input_A, Input_B);
  and and_1 (Carry_Out, Input_A, Input_B);
  or or_2 (or_2_out, Input_A_3, Input_B_3);
  and and_2 (and_2_out, Input_A_3, Input_B_3);
  and and_3 (Carry_Out_3, Input_A_3, Input_B_3);
  or or_3 (or_3_out, Input_A_5, Input_B_5);
  nand nand_1 (nand_1_out, Input_A_5, Input_B_5);
  and and_4 (Carry_Out_5, Input_A_5, Input_B_5);
  and and_5 (Output, or_1_out, not_1_out);
  not not_1 (not_1_out, Carry_Out);
  and and_6 (Output_3, or_2_out, not_2_out);
  not not_2 (not_2_out, and_2_out);
  and and_7 (Output_5, or_3_out, nand_1_out);
  xor xor_1 (Output_6, Input_A_6, Input_B_6);
  and and_8 (Carry_Out_6, Input_A_6, Input_B_6);
  nor nor_1 (nor_1_out, Input_A_2, Input_B_2);
  and and_9 (Carry_Out_2, Input_A_2, Input_B_2);
  nor nor_2 (nor_2_out, Input_A_4, Input_B_4);
  and and_10 (and_10_out, Input_A_4, Input_B_4);
  and and_11 (Carry_Out_4, Input_A_4, Input_B_4);
  nor nor_3 (Output_2, nor_1_out, Carry_Out_2);
  nor nor_4 (Output_4, nor_2_out, and_10_out);
  nor nor_5 (nor_5_out, A, B);
  and and_12 (and_12_out, A, B);
  xor xor_2 (out_22, A, B);
  or or_4 (or_4_out, A, B);
  nand nand_2 (nand_2_out, A, B);
  or or_5 (or_5_out, A, B);
  not not_3 (not_3_out, and_13_out);
  and and_13 (and_13_out, A, B);
  nor nor_6 (out_19, nor_5_out, and_12_out);
  and and_14 (out_25, or_4_out, nand_2_out);
  and and_15 (out_28, or_5_out, not_3_out);
endmodule

module ADD3 (
  input  R,
  input  R_2,
  input  A,
  input  A_2,
  input  in_5,
  input  B,
  input  B_2,
  input  in_8,
  input  in_9,
  input  R_3,
  input  R_4,
  input  A_3,
  input  A_4,
  input  B_3,
  input  B_4,
  input  R_5,
  input  R_6,
  input  A_5,
  input  A_6,
  input  B_5,
  input  B_6,
  input  R_7,
  input  R_8,
  input  A_7,
  input  A_8,
  input  B_7,
  input  B_8,
  output S,
  output S_2,
  output RS,
  output RS_2,
  output out_32,
  output out_33,
  output S_3,
  output S_4,
  output RS_3,
  output RS_4,
  output S_5,
  output S_6,
  output RS_5,
  output RS_6,
  output S_7,
  output S_8,
  output RS_7,
  output RS_8
);

  wire adder_1_cout, adder_1_out, adder_2_cout;

  Adder #(.width(1)) adder_1 (.a(in_8), .b(in_9), .out(adder_1_out), .cin(1'b0), .cout(adder_1_cout));
  Adder #(.width(1)) adder_2 (.a(in_5), .b(adder_1_out), .out(out_32), .cin(1'b0), .cout(adder_2_cout));
  or or_1 (out_33, adder_2_cout, adder_1_cout);
  Adder #(.width(1)) adder_3 (.a(A), .b(B), .out(S), .cin(R), .cout(RS));
  Adder #(.width(1)) adder_4 (.a(A_3), .b(B_3), .out(S_3), .cin(R_3), .cout(RS_3));
  Adder #(.width(1)) adder_5 (.a(A_5), .b(B_5), .out(S_5), .cin(R_5), .cout(RS_5));
  Adder #(.width(1)) adder_6 (.a(A_7), .b(B_7), .out(S_7), .cin(R_7), .cout(RS_7));
  Adder #(.width(1)) adder_7 (.a(A_2), .b(B_2), .out(S_2), .cin(R_2), .cout(RS_2));
  Adder #(.width(1)) adder_8 (.a(A_4), .b(B_4), .out(S_4), .cin(R_4), .cout(RS_4));
  Adder #(.width(1)) adder_9 (.a(A_6), .b(B_6), .out(S_6), .cin(R_6), .cout(RS_6));
  Adder #(.width(1)) adder_10 (.a(A_8), .b(B_8), .out(S_8), .cin(R_8), .cout(RS_8));
endmodule

module test (
  input  [3:0] in_1,
  input  [3:0] in_2,
  input  [3:0] in_3,
  input  [3:0] in_4,
  input  [3:0] in_5,
  input  [3:0] in_6,
  output [3:0] out_7,
  output [3:0] out_8,
  output [3:0] out_9
);

  wire sub1_1_carry_out, sub1_2_carry_out, sub1_3_carry_out, sub2_1_carry_out, sub2_2_carry_out,
       sub2_3_carry_out, subtractor_1_bout, subtractor_2_bout, subtractor_3_bout;

  // Probe on in_1
  // Probe on in_1
  // Probe on in_1
  // Probe on in_4
  // Probe on in_4
  // Probe on in_4
  Subtractor #(.width(1)) subtractor_1 (.a(in_1[0]), .b(in_4[0]), .out(out_7[0]), .bin(1'b0), .bout(subtractor_1_bout));
  Subtractor #(.width(1)) subtractor_2 (
    .a(in_1[1]), .b(in_4[1]), .out(out_7[1]), .bin(subtractor_1_bout), .bout(subtractor_2_bout));
  Subtractor #(.width(1)) subtractor_3 (
    .a(in_1[2]), .b(in_4[2]), .out(out_7[2]), .bin(subtractor_2_bout), .bout(subtractor_3_bout));
  Subtractor #(.width(1)) subtractor_4 (
    .a(in_1[3]), .b(in_4[3]), .out(out_7[3]), .bin(subtractor_3_bout));  // open: bout
  // Probe on out_7
  // Probe on out_7
  // Probe on out_7
  // Probe on in_2
  // Probe on in_2
  // Probe on in_2
  // Probe on in_5
  // Probe on in_5
  // Probe on in_5
  SUB1 sub1_1 (.Carry_In(1'b0), .Input_A(in_2[0]), .Input_B(in_5[0]), .Output(out_8[0]), .Carry_Out(sub1_1_carry_out));
  SUB1 sub1_2 (
    .Carry_In(sub1_1_carry_out), .Input_A(in_2[1]), .Input_B(in_5[1]), .Output(out_8[1]),
    .Carry_Out(sub1_2_carry_out));
  SUB1 sub1_3 (
    .Carry_In(sub1_2_carry_out), .Input_A(in_2[2]), .Input_B(in_5[2]), .Output(out_8[2]),
    .Carry_Out(sub1_3_carry_out));
  SUB1 sub1_4 (
    .Carry_In(sub1_3_carry_out), .Input_A(in_2[3]), .Input_B(in_5[3]), .Output(out_8[3]));  // open: Carry_Out
  // Probe on out_8
  // Probe on out_8
  // Probe on out_8
  // Probe on in_3
  // Probe on in_3
  // Probe on in_3
  // Probe on in_6
  // Probe on in_6
  // Probe on in_6
  SUB2 sub2_1 (.Carry_In(1'b0), .Input_A(in_3[0]), .Input_B(in_6[0]), .Output(out_9[0]), .Carry_Out(sub2_1_carry_out));
  SUB2 sub2_2 (
    .Carry_In(sub2_1_carry_out), .Input_A(in_3[1]), .Input_B(in_6[1]), .Output(out_9[1]),
    .Carry_Out(sub2_2_carry_out));
  SUB2 sub2_3 (
    .Carry_In(sub2_2_carry_out), .Input_A(in_3[2]), .Input_B(in_6[2]), .Output(out_9[2]),
    .Carry_Out(sub2_3_carry_out));
  SUB2 sub2_4 (
    .Carry_In(sub2_3_carry_out), .Input_A(in_3[3]), .Input_B(in_6[3]), .Output(out_9[3]));  // open: Carry_Out
  // Probe on out_9
  // Probe on out_9
  // Probe on out_9
endmodule
