// Logisim project 07_FLIP_FLOP_00_V.circ as structural Verilog: 16 circuits, main circuit main
module main (
  input  S,
  input  Clock,
  input  R,
  input  D,
  input  Clock_2,
  input  J,
  input  J_2,
  input  K,
  input  K_2,
  input  Clock_3,
  input  Clock_4,
  input  Clock_5,
  input  Clock_6,
  input  D_2,
  input  D_3,
  input  Clock_7,
  input  Clock_8,
  input  Clock_9,
  input  Clock_10,
  input  D_4,
  input  D_5,
  input  S_2,
  input  R_2,
  output out_24,
  output out_25,
  output out_26,
  output out_27,
  output out_28,
  output out_29,
  output out_30,
  output out_31,
  output out_32,
  output out_33,
  output out_34,
  output out_35,
  output out_36,
  output out_37,
  output out_38,
  output out_39,
  output out_40,
  output out_41,
  output out_42,
  output out_43,
  output out_44,
  output out_45
);

  S_R_Flip_Flop #(.trigger("high")) s_r_ff_1 (
    .S(S), .clk(Clock_2), .R(R), .Q(out_24), .preset(1'b0), .reset(1'b0), .en(1'b1));  // open: Qn
  J_K_Flip_Flop #(.trigger("falling")) j_k_ff_1 (
    .J(J), .clk(Clock_3), .K(K), .Q(out_28), .preset(1'b0), .en(1'b1), .reset(1'b0));  // open: Qn
  D_Flip_Flop #(.trigger("falling")) d_ff_1 (
    .clk(Clock_5), .D(D_2), .Q(out_32), .preset(1'b0), .en(1'b1), .reset(1'b0));  // open: Qn
  T_Flip_Flop #(.trigger("falling")) t_ff_1 (
    .clk(Clock_7), .T(1'b1), .Q(out_36), .preset(1'b0), .reset(1'b0), .en(1'b1));  // open: Qn
  T_Flip_Flop #(.trigger("falling")) t_ff_2 (
    .clk(Clock_9), .T(D_4), .Q(out_40), .preset(1'b0), .reset(1'b0), .en(1'b1));  // open: Qn
  S_R_Flip_Flop #(.trigger("high")) s_r_ff_2 (
    .S(S_2), .clk(1'b1), .R(R_2), .Q(out_44), .preset(1'b0), .reset(1'b0), .en(1'b1));  // open: Qn
  RSH rsh_1 (.S(S), .H(Clock_2), .R(R), .Q(out_25));  // open: Q_Not
  JKD jkd_1 (.J(J), .CLK(Clock_3), .K(K), .Q(out_29));  // open: QN
  DD dd_1 (.D(D_2), .H(Clock_5), .Q(out_33));  // open: QN
  TD td_1 (.H(Clock_7), .Q(out_37));  // open: QN
  TLD tld_1 (.T(D_4), .Q(out_41), .H(Clock_9));  // open: QN
  RS rs_1 (.R(R_2), .Q(out_45), .S(S_2));  // open: Q_Not
  D_Flip_Flop #(.trigger("high")) d_ff_2 (
    .clk(Clock), .D(D), .Q(out_26), .preset(1'b0), .en(1'b1), .reset(1'b0));  // open: Qn
  J_K_Flip_Flop j_k_ff_2 (
    .J(J_2), .clk(Clock_4), .K(K_2), .Q(out_30), .preset(1'b0), .en(1'b1), .reset(1'b0));  // open: Qn
  D_Flip_Flop d_ff_3 (.clk(Clock_6), .D(D_3), .Q(out_34), .preset(1'b0), .en(1'b1), .reset(1'b0));  // open: Qn
  T_Flip_Flop t_ff_3 (.clk(Clock_8), .T(1'b1), .Q(out_38), .preset(1'b0), .reset(1'b0), .en(1'b1));  // open: Qn
  T_Flip_Flop t_ff_4 (.clk(Clock_10), .T(D_5), .Q(out_42), .preset(1'b0), .reset(1'b0), .en(1'b1));  // open: Qn
  D d_1 (.D(D), .H(Clock), .Q(out_27));  // open: Q_Not
  JKM jkm_1 (.J(J_2), .CLK(Clock_4), .K(K_2), .Q(out_31));  // open: QN
  DM dm_1 (.D(D_3), .Q(out_35), .H(Clock_6));  // open: QN
  TM tm_1 (.Q(out_39), .H(Clock_8));  // open: QN
  TLM tlm_1 (.H(Clock_10), .Q(out_43), .T(D_5));  // open: QN
endmodule

module RS (
  input  R,
  input  S,
  output Q,
  output Q_Not
);

  nor nor_1 (Q, R, Q_Not);
  nor nor_2 (Q_Not, Q, S);
endmodule

module RS1 (
  input  S,
  input  R,
  output Q,
  output Q_Not
);

  wire not_1_out, not_2_out;

  not not_1 (not_1_out, S);
  nand nand_1 (Q, not_1_out, Q_Not);
  nand nand_2 (Q_Not, Q, not_2_out);
  not not_2 (not_2_out, R);
endmodule

module RSL (
  input  S,
  input  R,
  output Q,
  output Q_Not
);

  wire and_1_out, not_1_out;

  not not_1 (not_1_out, R);
  and and_1 (and_1_out, S, not_1_out);
  RS rs_1 (.R(R), .Q(Q), .Q_Not(Q_Not), .S(and_1_out));

  // Notes on the sheet:
  //   S0
  //   R0
endmodule

module RSH (
  input  S,
  input  H,
  input  R,
  output Q,
  output Q_Not
);

  wire and_1_out, and_2_out;

  and and_1 (and_1_out, S, H);
  and and_2 (and_2_out, H, R);
  RS rs_1 (.R(and_2_out), .Q(Q), .Q_Not(Q_Not), .S(and_1_out));

  // Notes on the sheet:
  //   S0
  //   R0
endmodule

module RSHB (
  input  S,
  input  H,
  input  R,
  output Q,
  output Q_Not
);

  wire not_1_out;

  not not_1 (not_1_out, H);
  RSH rsh_1 (.S(S), .H(not_1_out), .R(R), .Q(Q), .Q_Not(Q_Not));

  // Notes on the sheet:
  //   H: pull=down
  //   S: pull=down
  //   R: pull=down
endmodule

module RSHB1 (
  input  S,
  input  H,
  input  R,
  output Q,
  output Q_Not
);

  wire and_1_out, and_2_out, not_1_out;

  and and_1 (and_1_out, S, not_1_out);
  not not_1 (not_1_out, H);
  and and_2 (and_2_out, not_1_out, R);
  RS rs_1 (.R(and_2_out), .Q(Q), .Q_Not(Q_Not), .S(and_1_out));

  // Notes on the sheet:
  //   S0
  //   R0
endmodule

module D (
  input  D,
  input  H,
  output Q,
  output Q_Not
);

  wire not_1_out;

  RSH rsh_1 (.S(D), .H(H), .R(not_1_out), .Q(Q), .Q_Not(Q_Not));
  not not_1 (not_1_out, D);

  // Notes on the sheet:
  //   S0
  //   R0
endmodule

module JKD (
  input  J,
  input  CLK,
  input  K,
  output Q,
  output QN
);

  wire not_1_out, rsh_1_q, rsh_1_q_not;

  not not_1 (not_1_out, CLK);
  RSH rsh_1 (.S(J), .H(CLK), .R(K), .Q(rsh_1_q), .Q_Not(rsh_1_q_not));
  RSH rsh_2 (.S(rsh_1_q), .H(not_1_out), .R(rsh_1_q_not), .Q(Q), .Q_Not(QN));

  // Notes on the sheet:
  //   H1
  //   S1
  //   R1
  //   H2
  //   Q1
  //   S2
  //   R2
  //   RSH1
  //   Q2
  //   RSH2
endmodule

module JKM (
  input  J,
  input  CLK,
  input  K,
  output Q,
  output QN
);

  wire not_1_out, rsh_1_q, rsh_1_q_not;

  not not_1 (not_1_out, CLK);
  RSH rsh_1 (.S(J), .H(not_1_out), .R(K), .Q(rsh_1_q), .Q_Not(rsh_1_q_not));
  RSH rsh_2 (.S(rsh_1_q), .H(CLK), .R(rsh_1_q_not), .Q(Q), .Q_Not(QN));

  // Notes on the sheet:
  //   S1
  //   R1
  //   H1
  //   RSH1
  //   Q1
  //   S2
  //   R2
  //   H2
  //   RSH2
  //   Q2
endmodule

module DD (
  input  D,
  input  H,
  output Q,
  output QN
);

  wire not_1_out;

  not not_1 (not_1_out, D);
  JKD jkd_1 (.J(D), .CLK(H), .K(not_1_out), .Q(Q), .QN(QN));
endmodule

module DM (
  input  D,
  input  H,
  output Q,
  output QN
);

  wire not_1_out;

  not not_1 (not_1_out, D);
  JKM jkm_1 (.J(D), .CLK(H), .K(not_1_out), .Q(Q), .QN(QN));
endmodule

module TD (
  input  H,
  output Q,
  output QN
);

  D_Flip_Flop #(.trigger("falling")) d_ff_1 (.clk(H), .D(QN), .Q(Q), .Qn(QN), .preset(1'b0), .en(1'b1), .reset(1'b0));
endmodule

module TM (
  input  H,
  output Q,
  output QN
);

  D_Flip_Flop d_ff_1 (.clk(H), .D(QN), .Q(Q), .Qn(QN), .preset(1'b0), .en(1'b1), .reset(1'b0));
endmodule

module TLD (
  input  H,
  input  T,
  output Q,
  output QN
);

  wire and_1_out;

  and and_1 (and_1_out, H, T);
  D_Flip_Flop #(.trigger("falling")) d_ff_1 (
    .clk(and_1_out), .D(QN), .Q(Q), .Qn(QN), .preset(1'b0), .en(1'b1), .reset(1'b0));
endmodule

module TLM (
  input  H,
  input  T,
  output Q,
  output QN
);

  wire and_1_out;

  and and_1 (and_1_out, H, T);
  D_Flip_Flop d_ff_1 (.clk(and_1_out), .D(QN), .Q(Q), .Qn(QN), .preset(1'b0), .en(1'b1), .reset(1'b0));
endmodule
