// Logisim project 09_COUNTER_V.circ as structural Verilog
module main (
  input  count,
  input  enable,
  input  clear,
  input  choice,
  input  choise
);

  wire cmp4_1_carry, counter_1_carry, counter_3_carry, dcmp4_1_carry;
  wire [3:0] cmp4_1_output, cmp4_2_output, counter_1_q, counter_2_q;
  wire [7:0] counter_3_q, dcmp4_1_output;

  CMP4 cmp4_1 (.Clock(count), .Count(enable), .Clear(clear), .Output(cmp4_1_output), .Carry(cmp4_1_carry));
  Counter #(.width(4), .max('hf), .trigger("falling")) counter_1 (
    .load(choice), .D(4'b0000), .count(enable), .Q(counter_1_q), .carry(counter_1_carry), .clk(count),
    .clr(clear));
  Hex_Digit_Display hex_digit_display_1 (.value(cmp4_1_output));  // open: dp
  Hex_Digit_Display hex_digit_display_2 (.value(cmp4_2_output));  // open: dp
  Hex_Digit_Display hex_digit_display_3 (.value(counter_1_q));  // open: dp
  Hex_Digit_Display hex_digit_display_4 (.value(counter_2_q));  // open: dp
  CMP4 cmp4_2 (.Clock(cmp4_1_carry), .Count(count), .Clear(clear), .Output(cmp4_2_output));  // open: Carry
  Counter #(.width(4), .max('hf), .trigger("falling")) counter_2 (
    .load(choice), .D(4'b0000), .count(enable), .Q(counter_2_q), .clk(counter_1_carry), .clr(clear));  // open: carry
  // Probe on {cmp4_2_output, cmp4_1_output}
  // Probe on {cmp4_2_output, cmp4_1_output}
  // Probe on {cmp4_2_output, cmp4_1_output}
  // Probe on {cmp4_2_output, cmp4_1_output}
  // Probe on {counter_2_q, counter_1_q}
  // Probe on {counter_2_q, counter_1_q}
  // Probe on {counter_2_q, counter_1_q}
  // Probe on {counter_2_q, counter_1_q}
  Counter #(.width(4), .max('hf)) counter_3 (
    .load(choise), .D(4'b0000), .count(enable), .Q(counter_3_q[3:0]), .carry(counter_3_carry), .clk(count),
    .clr(clear));
  Hex_Digit_Display hex_digit_display_5 (.value(dcmp4_1_output[7:4]));  // open: dp
  Hex_Digit_Display hex_digit_display_6 (.value(dcmp4_1_output[3:0]));  // open: dp
  DCMP4 dcmp4_1 (.Clock(count), .Count(enable), .Clear(clear), .Output(dcmp4_1_output[3:0]), .Carry(dcmp4_1_carry));
  Hex_Digit_Display hex_digit_display_7 (.value(counter_3_q[3:0]));  // open: dp
  Hex_Digit_Display hex_digit_display_8 (.value(counter_3_q[7:4]));  // open: dp
  DCMP4 dcmp4_2 (.Clock(dcmp4_1_carry), .Count(enable), .Clear(clear), .Output(dcmp4_1_output[7:4]));  // open: Carry
  Counter #(.width(4), .max('hf), .trigger("falling")) counter_4 (
    .load(choise), .D(4'b0000), .count(enable), .Q(counter_3_q[7:4]), .clk(counter_3_carry), .clr(clear));  // open: carry
  // Probe on dcmp4_1_output
  // Probe on dcmp4_1_output
  // Probe on dcmp4_1_output
  // Probe on dcmp4_1_output
  // Probe on counter_3_q
  // Probe on counter_3_q
  // Probe on counter_3_q
  // Probe on counter_3_q
endmodule

module main1 (
  input  [3:0] in_1,
  input  in_2,
  input  Enable,
  input  in_4,
  input  Count,
  input  in_6,
  input  Clock,
  input  in_8,
  input  Clear,
  input  in_10,
  input  [3:0] Data,
  output [3:0] out_12,
  output out_13,
  output [3:0] out_14,
  output out_15,
  output [3:0] out_16,
  output out_17,
  output [3:0] out_18,
  output [3:0] out_19,
  output [3:0] out_20,
  output [3:0] out_21,
  output [3:0] out_22,
  output out_23,
  output out_24,
  output out_25,
  output out_26,
  output out_27
);

  CMP4D2 cmp4d2_1 (
    .Output(out_12), .Clock(in_6), .Carry(out_13), .Count(in_4), .Clear(in_8), .Choice(in_2), .in_5(in_1));
  DCMP4D dcmp4d_1 (
    .Output(out_14), .Clock(in_6), .Carry(out_15), .Count(in_4), .Clear(in_8), .Choice(in_2), .in_5(in_1));
  Counter #(.width(4), .max('hf)) counter_1 (
    .load(in_2), .D(in_1), .count(in_4), .Q(out_16), .carry(out_17), .clk(in_6), .clr(in_8));
  Counter #(.width(4), .max('hf)) counter_2 (
    .load(in_10), .D(in_1), .count(in_4), .Q(out_22), .carry(out_27), .clk(in_6), .clr(in_8));
  // Probe on out_12
  // Probe on out_12
  // Probe on out_12
  // Probe on out_14
  // Probe on out_14
  // Probe on out_14
  // Probe on out_16
  // Probe on out_16
  // Probe on out_16
  // Probe on out_22
  // Probe on out_22
  // Probe on out_22
  Counter #(.width(4), .max('hf)) counter_3 (
    .load(Enable), .D(Data), .count(Count), .Q(out_18), .carry(out_23), .clk(Clock), .clr(Clear));
  // Probe on out_18
  // Probe on out_18
  // Probe on out_18
  MCMP4 mcmp4_1 (
    .Output(out_19), .Clock(Clock), .Carry(out_24), .Count(Count), .Clear(Clear), .Choice(Enable), .in_5(Data));
  // Probe on out_19
  // Probe on out_19
  // Probe on out_19
  DCP4D2 dcp4d2_1 (
    .Clock(Clock), .Count(Count), .Clear(Clear), .Choice(Enable), .in_5(Data), .Output(out_20), .Carry(out_25));
  // Probe on out_20
  // Probe on out_20
  // Probe on out_20
  DCP4D3 dcp4d3_1 (
    .Clock(Clock), .Count(Count), .Clear(Clear), .Choice(Enable), .in_5(Data), .Output(out_21), .Carry(out_26));
  // Probe on out_21
  // Probe on out_21
  // Probe on out_21
endmodule

module CMP4 (
  input  Clock,
  input  Count,
  input  Clear,
  output [3:0] Output,
  output Carry
);

  wire d_ff_1_qn, d_ff_2_qn, d_ff_3_qn, d_ff_4_qn;

  D_Flip_Flop #(.trigger("falling")) d_ff_1 (
    .clk(Clock), .D(d_ff_1_qn), .Q(Output[0]), .Qn(d_ff_1_qn), .preset(1'b0), .en(Count), .reset(Clear));
  D_Flip_Flop #(.trigger("falling")) d_ff_2 (
    .clk(Output[1]), .D(d_ff_2_qn), .Q(Output[2]), .Qn(d_ff_2_qn), .preset(1'b0), .en(Count), .reset(Clear));
  D_Flip_Flop #(.trigger("falling")) d_ff_3 (
    .clk(Output[0]), .D(d_ff_3_qn), .Q(Output[1]), .Qn(d_ff_3_qn), .preset(1'b0), .en(Count), .reset(Clear));
  D_Flip_Flop #(.trigger("falling")) d_ff_4 (
    .clk(Output[2]), .D(d_ff_4_qn), .Q(Carry), .Qn(d_ff_4_qn), .preset(1'b0), .en(Count), .reset(Clear));

  assign Output[3] = Carry;

  // Notes on the sheet:
  //   D0
  //   Q0
  //   D1
  //   Q2
  //   Q1
  //   D2
  //   Q3
  //   D3
endmodule

module DCMP4 (
  input  Clock,
  input  Count,
  input  Clear,
  output [3:0] Output,
  output Carry
);

  wire d_ff_1_qn, d_ff_2_qn, d_ff_3_qn, d_ff_4_qn;

  D_Flip_Flop d_ff_1 (
    .clk(Clock), .D(d_ff_1_qn), .Q(Output[0]), .Qn(d_ff_1_qn), .preset(1'b0), .en(Count), .reset(Clear));
  D_Flip_Flop d_ff_2 (
    .clk(Output[0]), .D(d_ff_2_qn), .Q(Output[1]), .Qn(d_ff_2_qn), .preset(1'b0), .en(Count), .reset(Clear));
  D_Flip_Flop d_ff_3 (
    .clk(Output[1]), .D(d_ff_3_qn), .Q(Output[2]), .Qn(d_ff_3_qn), .preset(1'b0), .en(Count), .reset(Clear));
  D_Flip_Flop d_ff_4 (
    .clk(Output[2]), .D(d_ff_4_qn), .Q(Carry), .Qn(d_ff_4_qn), .preset(1'b0), .en(Count), .reset(Clear));

  assign Output[3] = Carry;

  // Notes on the sheet:
  //   D0
  //   Q0
  //   D1
  //   Q1
  //   D2
  //   Q3
  //   Q2
  //   D3
endmodule

module CMP4D (
  input  Clock,
  input  Count,
  input  Clear,
  input  Choice,
  input  [3:0] in_5,
  output [3:0] Output,
  output Carry
);

  wire and_1_out, and_4_out, d_ff_1_qn, d_ff_2_qn, d_ff_3_qn, d_ff_4_qn, not_1_out, not_2_out, not_4_out,
       not_5_out, or_1_out, or_2_out, or_3_out, or_4_out;
  wire [3:0] and_2_out, and_3_out, bit_extender_1_out, not_3_out;

  not not_1 (not_1_out, Clear);
  and and_1 (and_1_out, Clock, not_1_out, Choice, not_2_out);
  not not_2 (not_2_out, Count);
  assign bit_extender_1_out = {{3{and_1_out}}, and_1_out};  // Bit_Extender bit_extender_1
  assign and_2_out = bit_extender_1_out & in_5;  // AND_Gate and_2, 4 bits wide
  assign and_3_out = bit_extender_1_out & not_3_out;  // AND_Gate and_3, 4 bits wide
  assign not_3_out = ~in_5;  // NOT_Gate not_3, 4 bits wide
  not not_4 (not_4_out, Clock);
  and and_4 (and_4_out, Clear, not_5_out);
  not not_5 (not_5_out, and_1_out);
  D_Flip_Flop #(.trigger("falling")) d_ff_1 (
    .clk(not_4_out), .D(d_ff_1_qn), .Q(Output[0]), .Qn(d_ff_1_qn), .preset(and_2_out[0]), .en(Count),
    .reset(or_1_out));
  or or_1 (or_1_out, and_4_out, and_3_out[0]);
  D_Flip_Flop #(.trigger("falling")) d_ff_2 (
    .clk(Output[0]), .D(d_ff_2_qn), .Q(Output[1]), .Qn(d_ff_2_qn), .preset(and_2_out[1]), .en(Count),
    .reset(or_2_out));
  or or_2 (or_2_out, and_4_out, and_3_out[1]);
  D_Flip_Flop #(.trigger("falling")) d_ff_3 (
    .clk(Output[1]), .D(d_ff_3_qn), .Q(Output[2]), .Qn(d_ff_3_qn), .preset(and_2_out[2]), .en(Count),
    .reset(or_3_out));
  or or_3 (or_3_out, and_4_out, and_3_out[2]);
  D_Flip_Flop #(.trigger("falling")) d_ff_4 (
    .clk(Output[2]), .D(d_ff_4_qn), .Q(Carry), .Qn(d_ff_4_qn), .preset(and_2_out[3]), .en(Count),
    .reset(or_4_out));
  or or_4 (or_4_out, and_4_out, and_3_out[3]);

  assign Output[3] = Carry;

  // Notes on the sheet:
  //   Q0
  //   D0
  //   Q1
  //   D2
  //   D1
  //   Q2
  //   D3
  //   Q3
endmodule

module DCMP4D (
  input  Clock,
  input  Count,
  input  Clear,
  input  Choice,
  input  [3:0] in_5,
  output [3:0] Output,
  output Carry
);

  wire and_1_out, and_4_out, d_ff_1_qn, d_ff_2_qn, d_ff_3_qn, d_ff_4_qn, not_1_out, not_2_out, not_4_out,
       or_1_out, or_2_out, or_3_out, or_4_out;
  wire [3:0] and_2_out, and_3_out, bit_extender_1_out, not_3_out;

  not not_1 (not_1_out, Clear);
  and and_1 (and_1_out, Clock, not_1_out, Choice, not_2_out);
  not not_2 (not_2_out, Count);
  assign bit_extender_1_out = {{3{and_1_out}}, and_1_out};  // Bit_Extender bit_extender_1
  assign and_2_out = bit_extender_1_out & in_5;  // AND_Gate and_2, 4 bits wide
  assign and_3_out = bit_extender_1_out & not_3_out;  // AND_Gate and_3, 4 bits wide
  assign not_3_out = ~in_5;  // NOT_Gate not_3, 4 bits wide
  and and_4 (and_4_out, Clear, not_4_out);
  not not_4 (not_4_out, and_1_out);
  D_Flip_Flop d_ff_1 (
    .clk(Clock), .D(d_ff_1_qn), .Q(Output[0]), .Qn(d_ff_1_qn), .preset(and_2_out[0]), .en(Count),
    .reset(or_1_out));
  or or_1 (or_1_out, and_4_out, and_3_out[0]);
  D_Flip_Flop d_ff_2 (
    .clk(Output[0]), .D(d_ff_2_qn), .Q(Output[1]), .Qn(d_ff_2_qn), .preset(and_2_out[1]), .en(Count),
    .reset(or_2_out));
  or or_2 (or_2_out, and_4_out, and_3_out[1]);
  D_Flip_Flop d_ff_3 (
    .clk(Output[1]), .D(d_ff_3_qn), .Q(Output[2]), .Qn(d_ff_3_qn), .preset(and_2_out[2]), .en(Count),
    .reset(or_3_out));
  or or_3 (or_3_out, and_4_out, and_3_out[2]);
  D_Flip_Flop d_ff_4 (
    .clk(Output[2]), .D(d_ff_4_qn), .Q(Carry), .Qn(d_ff_4_qn), .preset(and_2_out[3]), .en(Count),
    .reset(or_4_out));
  or or_4 (or_4_out, and_4_out, and_3_out[3]);

  assign Output[3] = Carry;

  // Notes on the sheet:
  //   Q0
  //   D0
  //   Q1
  //   D2
  //   D1
  //   Q2
  //   D3
  //   Q3
endmodule

module MCMP4 (
  input  Clock,
  input  Count,
  input  Clear,
  input  Choice,
  input  [3:0] in_5,
  output [3:0] Output,
  output Carry
);

  wire and_1_out, and_4_out, and_6_out, and_8_out, d_ff_1_qn, d_ff_2_qn, d_ff_3_qn, d_ff_4_qn, d_ff_5_qn,
       d_ff_6_qn, d_ff_7_qn, d_ff_8_qn, not_2_out, not_3_out, not_4_out, not_5_out, not_6_out, or_1_out,
       or_2_out, or_3_out, or_4_out;
  wire [3:0] and_2_out, and_3_out, and_5_out, and_7_out, bit_extender_1_out, bit_extender_2_out,
       bit_extender_3_out, d_ff_1_q, d_ff_2_q, not_1_out;

  assign bit_extender_1_out = {{3{and_1_out}}, and_1_out};  // Bit_Extender bit_extender_1
  assign not_1_out = ~in_5;  // NOT_Gate not_1, 4 bits wide
  not not_2 (not_2_out, Clear);
  and and_1 (and_1_out, Clock, not_2_out, Choice, not_3_out);
  not not_3 (not_3_out, Count);
  assign and_2_out = bit_extender_1_out & in_5;  // AND_Gate and_2, 4 bits wide
  assign and_3_out = bit_extender_1_out & not_1_out;  // AND_Gate and_3, 4 bits wide
  and and_4 (and_4_out, Clear, not_4_out);
  not not_4 (not_4_out, and_1_out);
  or or_1 (or_1_out, and_4_out, and_3_out[0]);
  or or_2 (or_2_out, and_4_out, and_3_out[1]);
  or or_3 (or_3_out, and_4_out, and_3_out[2]);
  not not_5 (not_5_out, Clock);
  or or_4 (or_4_out, and_4_out, and_3_out[3]);
  D_Flip_Flop #(.trigger("falling")) d_ff_1 (
    .clk(not_5_out), .D(d_ff_1_qn), .Q(d_ff_1_q[0]), .Qn(d_ff_1_qn), .preset(and_2_out[0]), .en(Count),
    .reset(or_1_out));
  D_Flip_Flop d_ff_2 (
    .clk(Clock), .D(d_ff_2_qn), .Q(d_ff_2_q[0]), .Qn(d_ff_2_qn), .preset(and_2_out[0]), .en(Count),
    .reset(or_1_out));
  D_Flip_Flop #(.trigger("falling")) d_ff_3 (
    .clk(d_ff_1_q[0]), .D(d_ff_3_qn), .Q(d_ff_1_q[1]), .Qn(d_ff_3_qn), .preset(and_2_out[1]), .en(Count),
    .reset(or_2_out));
  D_Flip_Flop d_ff_4 (
    .clk(d_ff_2_q[0]), .D(d_ff_4_qn), .Q(d_ff_2_q[1]), .Qn(d_ff_4_qn), .preset(and_2_out[1]), .en(Count),
    .reset(or_2_out));
  D_Flip_Flop #(.trigger("falling")) d_ff_5 (
    .clk(d_ff_1_q[1]), .D(d_ff_5_qn), .Q(d_ff_1_q[2]), .Qn(d_ff_5_qn), .preset(and_2_out[2]), .en(Count),
    .reset(or_3_out));
  D_Flip_Flop #(.trigger("falling")) d_ff_6 (
    .clk(d_ff_1_q[2]), .D(d_ff_6_qn), .Q(d_ff_1_q[3]), .Qn(d_ff_6_qn), .preset(and_2_out[3]), .en(Count),
    .reset(or_4_out));
  D_Flip_Flop d_ff_7 (
    .clk(d_ff_2_q[1]), .D(d_ff_7_qn), .Q(d_ff_2_q[2]), .Qn(d_ff_7_qn), .preset(and_2_out[2]), .en(Count),
    .reset(or_3_out));
  D_Flip_Flop d_ff_8 (
    .clk(d_ff_2_q[2]), .D(d_ff_8_qn), .Q(d_ff_2_q[3]), .Qn(d_ff_8_qn), .preset(and_2_out[3]), .en(Count),
    .reset(or_4_out));
  assign and_5_out = d_ff_1_q & bit_extender_2_out;  // AND_Gate and_5, 4 bits wide
  assign bit_extender_2_out = {{3{not_6_out}}, not_6_out};  // Bit_Extender bit_extender_2
  and and_6 (and_6_out, d_ff_1_q[3], not_6_out);
  not not_6 (not_6_out, Choice);
  assign and_7_out = d_ff_2_q & bit_extender_3_out;  // AND_Gate and_7, 4 bits wide
  assign bit_extender_3_out = {{3{Choice}}, Choice};  // Bit_Extender bit_extender_3
  and and_8 (and_8_out, d_ff_2_q[3], Choice);
  assign Output = and_5_out | and_7_out;  // OR_Gate or_5, 4 bits wide
  or or_6 (Carry, and_6_out, and_8_out);

  // Notes on the sheet:
  //   D0
  //   D0
  //   Q0
  //   D1
  //   Q0
  //   D1
  //   Q1
  //   D2
  //   Q1
  //   D2
  //   Q2
  //   D3
  //   Q2
  //   D3
  //   Q3
  //   Q3
endmodule

module PCM1BD (
  input  Clock,
  input  Enable,
  input  Place,
  input  Data,
  input  Clear,
  output Q
);

  wire and_1_out, and_2_out, d_ff_1_qn, not_1_out, or_1_out;

  and and_1 (and_1_out, Place, Data);
  and and_2 (and_2_out, Place, not_1_out);
  not not_1 (not_1_out, Data);
  D_Flip_Flop #(.trigger("falling")) d_ff_1 (
    .clk(Clock), .D(d_ff_1_qn), .Q(Q), .Qn(d_ff_1_qn), .preset(and_1_out), .en(Enable), .reset(or_1_out));
  or or_1 (or_1_out, and_2_out, Clear);

  // Notes on the sheet:
  //   D0
endmodule

module CMP4D2 (
  input  Clock,
  input  Count,
  input  Clear,
  input  Choice,
  input  [3:0] in_5,
  output [3:0] Output,
  output Carry
);

  wire and_1_out, not_1_out, not_2_out, not_3_out;

  not not_1 (not_1_out, Clear);
  and and_1 (and_1_out, Clock, not_1_out, Choice, not_2_out);
  not not_2 (not_2_out, Count);
  not not_3 (not_3_out, Clock);
  PCM1BD pcm1bd_1 (.Clock(not_3_out), .Enable(Count), .Place(and_1_out), .Data(in_5[0]), .Clear(Clear), .Q(Output[0]));
  PCM1BD pcm1bd_2 (.Clock(Output[0]), .Enable(Count), .Place(and_1_out), .Data(in_5[1]), .Clear(Clear), .Q(Output[1]));
  PCM1BD pcm1bd_3 (.Clock(Output[1]), .Enable(Count), .Place(and_1_out), .Data(in_5[2]), .Clear(Clear), .Q(Output[2]));
  PCM1BD pcm1bd_4 (.Clock(Output[2]), .Enable(Count), .Place(and_1_out), .Data(in_5[3]), .Clear(Clear), .Q(Carry));

  assign Output[3] = Carry;
endmodule

module PDM1BD (
  input  Clock,
  input  Enable,
  input  Place,
  input  Data,
  input  Clear,
  output Q
);

  wire and_1_out, and_2_out, d_ff_1_qn, not_1_out, or_1_out;

  and and_1 (and_1_out, Place, Data);
  and and_2 (and_2_out, Place, not_1_out);
  not not_1 (not_1_out, Data);
  D_Flip_Flop d_ff_1 (
    .clk(Clock), .D(d_ff_1_qn), .Q(Q), .Qn(d_ff_1_qn), .preset(and_1_out), .en(Enable), .reset(or_1_out));
  or or_1 (or_1_out, and_2_out, Clear);

  // Notes on the sheet:
  //   D0
endmodule

module DMP4D2 (
  input  Clock,
  input  Count,
  input  Clear,
  input  Choice,
  input  [3:0] in_5,
  output [3:0] Output,
  output Carry
);

  wire and_1_out, not_1_out, not_2_out;

  not not_1 (not_1_out, Clear);
  and and_1 (and_1_out, Clock, not_1_out, Choice, not_2_out);
  not not_2 (not_2_out, Count);
  PDM1BD pdm1bd_1 (.Clock(Clock), .Enable(Count), .Place(and_1_out), .Data(in_5[0]), .Clear(Clear), .Q(Output[0]));
  PDM1BD pdm1bd_2 (.Clock(Output[0]), .Enable(Count), .Place(and_1_out), .Data(in_5[1]), .Clear(Clear), .Q(Output[1]));
  PDM1BD pdm1bd_3 (.Clock(Output[1]), .Enable(Count), .Place(and_1_out), .Data(in_5[2]), .Clear(Clear), .Q(Output[2]));
  PDM1BD pdm1bd_4 (.Clock(Output[2]), .Enable(Count), .Place(and_1_out), .Data(in_5[3]), .Clear(Clear), .Q(Carry));

  assign Output[3] = Carry;
endmodule

module PDC1BD (
  input  Clock,
  input  Enable,
  input  Place,
  input  Data,
  input  Clear,
  input  Countdown,
  output Q
);

  wire and_1_out, and_2_out, and_3_out, and_4_out, d_ff_1_q, d_ff_1_qn, d_ff_2_q, d_ff_2_qn, not_1_out,
       not_2_out, or_1_out;

  and and_1 (and_1_out, Place, Data);
  and and_2 (and_2_out, Place, not_1_out);
  not not_1 (not_1_out, Data);
  or or_1 (or_1_out, and_2_out, Clear);
  D_Flip_Flop #(.trigger("falling")) d_ff_1 (
    .clk(Clock), .D(d_ff_1_qn), .Q(d_ff_1_q), .Qn(d_ff_1_qn), .preset(and_1_out), .en(Enable),
    .reset(or_1_out));
  D_Flip_Flop d_ff_2 (
    .clk(Clock), .D(d_ff_2_qn), .Q(d_ff_2_q), .Qn(d_ff_2_qn), .preset(and_1_out), .en(Enable),
    .reset(or_1_out));
  and and_3 (and_3_out, d_ff_1_q, not_2_out);
  not not_2 (not_2_out, Countdown);
  and and_4 (and_4_out, Countdown, d_ff_2_q);
  or or_2 (Q, and_3_out, and_4_out);
endmodule

module DCP4D2 (
  input  Clock,
  input  Count,
  input  Clear,
  input  Choice,
  input  [3:0] in_5,
  output [3:0] Output,
  output Carry
);

  wire and_1_out, and_2_out, nor_1_out, not_1_out, not_2_out, or_1_out;

  and and_1 (and_1_out, Clock, Choice);
  or or_1 (or_1_out, and_1_out, nor_1_out);
  nor nor_1 (nor_1_out, Clock, Choice);
  not not_1 (not_1_out, Clear);
  not not_2 (not_2_out, Count);
  PDC1BD pdc1bd_1 (
    .Clock(or_1_out), .Enable(Count), .Place(and_2_out), .Data(in_5[0]), .Clear(Clear), .Countdown(Choice),
    .Q(Output[0]));
  and and_2 (and_2_out, Clock, not_1_out, Choice, not_2_out);
  PDC1BD pdc1bd_2 (
    .Clock(Output[0]), .Enable(Count), .Place(and_2_out), .Data(in_5[1]), .Clear(Clear), .Countdown(Choice),
    .Q(Output[1]));
  PDC1BD pdc1bd_3 (
    .Clock(Output[1]), .Enable(Count), .Place(and_2_out), .Data(in_5[2]), .Clear(Clear), .Countdown(Choice),
    .Q(Output[2]));
  PDC1BD pdc1bd_4 (
    .Clock(Output[2]), .Enable(Count), .Place(and_2_out), .Data(in_5[3]), .Clear(Clear), .Countdown(Choice),
    .Q(Carry));

  assign Output[3] = Carry;
endmodule

module DCP4D3 (
  input  Clock,
  input  Count,
  input  Clear,
  input  Choice,
  input  [3:0] in_5,
  output [3:0] Output,
  output Carry
);

  wire c4o_1_clock_2, c4o_1_place;

  C4O c4o_1 (
    .Clock(Clock), .Clear(Clear), .Choice(Choice), .Count(Count), .Clock_2(c4o_1_clock_2), .Place(c4o_1_place));
  PDC1BD pdc1bd_1 (
    .Clock(c4o_1_clock_2), .Enable(Count), .Place(c4o_1_place), .Data(in_5[0]), .Clear(Clear),
    .Countdown(Choice), .Q(Output[0]));
  PDC1BD pdc1bd_2 (
    .Clock(Output[0]), .Enable(Count), .Place(c4o_1_place), .Data(in_5[1]), .Clear(Clear),
    .Countdown(Choice), .Q(Output[1]));
  PDC1BD pdc1bd_3 (
    .Clock(Output[1]), .Enable(Count), .Place(c4o_1_place), .Data(in_5[2]), .Clear(Clear),
    .Countdown(Choice), .Q(Output[2]));
  PDC1BD pdc1bd_4 (
    .Clock(Output[2]), .Enable(Count), .Place(c4o_1_place), .Data(in_5[3]), .Clear(Clear),
    .Countdown(Choice), .Q(Carry));

  assign Output[3] = Carry;
endmodule

module PDC4BD (
  input  Clock,
  input  Place,
  input  Enable,
  input  Countdown,
  input  Clear,
  input  [3:0] Data,
  output [3:0] Output,
  output Carry
);

  PDC1BD pdc1bd_1 (
    .Clock(Clock), .Enable(Enable), .Place(Place), .Data(Data[0]), .Clear(Clear), .Countdown(Countdown),
    .Q(Output[0]));
  PDC1BD pdc1bd_2 (
    .Clock(Output[0]), .Enable(Enable), .Place(Place), .Data(Data[1]), .Clear(Clear), .Countdown(Countdown),
    .Q(Output[1]));
  PDC1BD pdc1bd_3 (
    .Clock(Output[1]), .Enable(Enable), .Place(Place), .Data(Data[2]), .Clear(Clear), .Countdown(Countdown),
    .Q(Output[2]));
  PDC1BD pdc1bd_4 (
    .Clock(Output[2]), .Enable(Enable), .Place(Place), .Data(Data[3]), .Clear(Clear), .Countdown(Countdown),
    .Q(Carry));

  assign Output[3] = Carry;
endmodule

module DCP4D4 (
  input  Clock,
  input  Count,
  input  Clear,
  input  Choice,
  input  [3:0] in_5,
  output [3:0] Output,
  output Carry
);

  wire c4o_1_clock_2, c4o_1_place;

  C4O c4o_1 (
    .Clock(Clock), .Clear(Clear), .Choice(Choice), .Count(Count), .Clock_2(c4o_1_clock_2), .Place(c4o_1_place));
  PDC4BD pdc4bd_1 (
    .Clock(c4o_1_clock_2), .Place(c4o_1_place), .Enable(Count), .Countdown(Choice), .Clear(Clear),
    .Data(in_5), .Output(Output), .Carry(Carry));
endmodule

module DCP8D3 (
  input  Clock,
  input  Count,
  input  Clear,
  input  Choice,
  input  [7:0] in_5,
  output [7:0] Output,
  output Carry
);

  wire c4o_1_clock_2, c4o_1_place;

  C4O c4o_1 (
    .Clock(Clock), .Clear(Clear), .Choice(Choice), .Count(Count), .Clock_2(c4o_1_clock_2), .Place(c4o_1_place));
  PDC1BD pdc1bd_1 (
    .Clock(c4o_1_clock_2), .Enable(Count), .Place(c4o_1_place), .Data(in_5[0]), .Clear(Clear),
    .Countdown(Choice), .Q(Output[0]));
  PDC1BD pdc1bd_2 (
    .Clock(Output[0]), .Enable(Count), .Place(c4o_1_place), .Data(in_5[1]), .Clear(Clear),
    .Countdown(Choice), .Q(Output[1]));
  PDC1BD pdc1bd_3 (
    .Clock(Output[1]), .Enable(Count), .Place(c4o_1_place), .Data(in_5[2]), .Clear(Clear),
    .Countdown(Choice), .Q(Output[2]));
  PDC1BD pdc1bd_4 (
    .Clock(Output[2]), .Enable(Count), .Place(c4o_1_place), .Data(in_5[3]), .Clear(Clear),
    .Countdown(Choice), .Q(Output[3]));
  PDC1BD pdc1bd_5 (
    .Clock(Output[3]), .Enable(Count), .Place(c4o_1_place), .Data(in_5[4]), .Clear(Clear),
    .Countdown(Choice), .Q(Output[4]));
  PDC1BD pdc1bd_6 (
    .Clock(Output[4]), .Enable(Count), .Place(c4o_1_place), .Data(in_5[5]), .Clear(Clear),
    .Countdown(Choice), .Q(Output[5]));
  PDC1BD pdc1bd_7 (
    .Clock(Output[5]), .Enable(Count), .Place(c4o_1_place), .Data(in_5[6]), .Clear(Clear),
    .Countdown(Choice), .Q(Output[6]));
  PDC1BD pdc1bd_8 (
    .Clock(Output[6]), .Enable(Count), .Place(c4o_1_place), .Data(in_5[7]), .Clear(Clear),
    .Countdown(Choice), .Q(Carry));

  assign Output[7] = Carry;
endmodule

module C4O (
  input  Clock,
  input  Clear,
  input  Choice,
  input  Count,
  output Clock_2,
  output Place
);

  wire and_1_out, nor_1_out, not_1_out, not_2_out;

  and and_1 (and_1_out, Clock, Choice);
  or or_1 (Clock_2, and_1_out, nor_1_out);
  nor nor_1 (nor_1_out, Clock, Choice);
  not not_1 (not_1_out, Clear);
  and and_2 (Place, Clock, not_1_out, Choice, not_2_out);
  not not_2 (not_2_out, Count);
endmodule

module DCP8D4 (
  input  Clock,
  input  Count,
  input  Clear,
  input  Choice,
  input  [7:0] in_5,
  output [7:0] Output,
  output Carry
);

  wire c4o_1_clock_2, c4o_1_place, pdc4bd_1_carry;

  C4O c4o_1 (
    .Clock(Clock), .Clear(Clear), .Choice(Choice), .Count(Count), .Clock_2(c4o_1_clock_2), .Place(c4o_1_place));
  PDC4BD pdc4bd_1 (
    .Clock(c4o_1_clock_2), .Place(c4o_1_place), .Enable(Count), .Countdown(Choice), .Clear(Clear),
    .Data(in_5[3:0]), .Output(Output[3:0]), .Carry(pdc4bd_1_carry));
  PDC4BD pdc4bd_2 (
    .Clock(pdc4bd_1_carry), .Place(c4o_1_place), .Enable(Count), .Countdown(Choice), .Clear(Clear),
    .Data(in_5[7:4]), .Output(Output[7:4]), .Carry(Carry));
endmodule

module PDC8BD (
  input  Clock,
  input  Place,
  input  Enable,
  input  Countdown,
  input  Clear,
  input  [7:0] Data,
  output [7:0] Output,
  output Carry
);

  wire pdc4bd_1_carry;

  PDC4BD pdc4bd_1 (
    .Clock(Clock), .Place(Place), .Enable(Enable), .Countdown(Countdown), .Clear(Clear), .Data(Data[3:0]),
    .Output(Output[3:0]), .Carry(pdc4bd_1_carry));
  PDC4BD pdc4bd_2 (
    .Clock(pdc4bd_1_carry), .Place(Place), .Enable(Enable), .Countdown(Countdown), .Clear(Clear),
    .Data(Data[7:4]), .Output(Output[7:4]), .Carry(Carry));
endmodule

module DCP8D5 (
  input  Clock,
  input  Count,
  input  Clear,
  input  Choice,
  input  [7:0] in_5,
  output [7:0] Output,
  output Carry
);

  wire c4o_1_clock_2, c4o_1_place;

  C4O c4o_1 (
    .Clock(Clock), .Clear(Clear), .Choice(Choice), .Count(Count), .Clock_2(c4o_1_clock_2), .Place(c4o_1_place));
  PDC8BD pdc8bd_1 (
    .Clock(c4o_1_clock_2), .Place(c4o_1_place), .Enable(Count), .Countdown(Choice), .Clear(Clear),
    .Data(in_5), .Output(Output), .Carry(Carry));
endmodule
