// Logisim project other.circ as structural Verilog: 2 circuits, main circuit main
module main (
  input  Buffer,
  input  in_2,
  input  in_3,
  input  in_4,
  input  in_5,
  input  [2:0] in_6,
  input  [2:0] in_7,
  input  [3:0] in_8,
  input  [3:0] Data,
  input  Load,
  input  Shift,
  input  Input,
  input  Clock,
  input  Clear,
  output out_15,
  output out_16,
  output out_17,
  output out_18,
  output out_19,
  output out_20,
  output out_21,
  output out_22,
  output out_23,
  output out_24,
  output out_25,
  output out_26,
  output out_27,
  output out_28,
  output [3:0] out_29
);

  wire not_1_out, xor_1_out, xor_2_out, xor_3_out, xor_4_out, xor_6_out, xor_9_out, xor_10_out;

  buf buffer_1 (out_15, Buffer);
  xor xor_1 (xor_1_out, in_7[0], in_7[1]);
  xor xor_2 (xor_2_out, in_8[0], in_8[1]);
  xor xor_3 (xor_3_out, in_8[0], in_8[1]);
  xor xor_4 (xor_4_out, in_8[2], in_8[3]);
  Pull_Resistor pull_resistor_1 (.node(out_16));
  assign out_16 = in_4 ? in_2 : 1'bz;  // Controlled_Buffer controlled_buffer_1
  and and_1 (out_19, in_2, in_4);
  xor odd_parity_1 (out_22, in_7[0], in_7[1], in_7[2]);
  xor xor_5 (out_23, xor_1_out, in_7[2]);
  xor odd_parity_2 (out_25, in_8[0], in_8[1], in_8[2], in_8[3]);
  xor xor_6 (xor_6_out, xor_2_out, in_8[2]);
  xor xor_7 (out_26, xor_6_out, in_8[3]);
  xor xor_8 (out_27, xor_3_out, xor_4_out);
  Shift_Register #(.length(4)) shift_register_1 (
    .shift(Shift), .in(Input), .clk(Clock), .out(out_28), .load(Load), .clr(Clear), .d0(Data[3]),
    .q0(out_29[3]), .d1(Data[2]), .q1(out_29[2]), .d2(Data[1]), .q2(out_29[1]), .d3(Data[0]), .q3(out_29[0]));
  not not_1 (not_1_out, in_3);
  xor xor_9 (xor_9_out, in_6[0], in_6[1]);
  assign out_17 = in_5 ? ~in_3 : 1'bz;  // Controlled_Inverter controlled_inverter_1
  Pull_Resistor pull_resistor_2 (.node(out_17));
  and and_2 (out_20, not_1_out, in_5);
  xnor even_parity_1 (out_21, in_6[0], in_6[1], in_6[2]);
  not not_2 (out_24, xor_10_out);
  xor xor_10 (xor_10_out, xor_9_out, in_6[2]);

  assign out_18 = Buffer;

  // Notes on the sheet:
  //   Odd Parity
  //   Odd Parity
  //   Controlled Buffer
  //   Controlled Inverter
  //   Even Parity
endmodule

module main2 (
  input  [2:0] in_1,
  input  [3:0] in_2,
  output [1:0] out_3,
  output [2:0] out_4
);

  BitAdder #(.width(3)) bitadder_1 (.in0(in_1), .out(out_3));
  BitAdder #(.width(4)) bitadder_2 (.in0(in_2), .out(out_4));
endmodule
